// Logisim project Atividade-1-3Trim-HugoBilleMartins.circ as structural Verilog: 2 circuits, main circuit main
module main (
  input  A,
  input  B,
  input  C,
  input  d,
  input  e,
  input  f,
  input  g,
  input  h,
  input  i,
  input  j,
  input  k,
  output out_12
);

  wire \mux2x1_1_saída , \mux2x1_2_saída , \mux2x1_3_saída , \mux2x1_4_saída , \mux2x1_5_saída ,
       \mux2x1_6_saída ;

  MUX2x1 mux2x1_1 (.a(d), .b(e), .Sel(A), .\Saída (\mux2x1_1_saída ));
  MUX2x1 mux2x1_2 (.a(f), .b(g), .Sel(A), .\Saída (\mux2x1_2_saída ));
  MUX2x1 mux2x1_3 (.a(h), .b(i), .Sel(A), .\Saída (\mux2x1_3_saída ));
  MUX2x1 mux2x1_4 (.a(j), .b(k), .Sel(A), .\Saída (\mux2x1_4_saída ));
  MUX2x1 mux2x1_5 (.a(\mux2x1_1_saída ), .b(\mux2x1_2_saída ), .Sel(B), .\Saída (\mux2x1_5_saída ));
  MUX2x1 mux2x1_6 (.a(\mux2x1_3_saída ), .b(\mux2x1_4_saída ), .Sel(B), .\Saída (\mux2x1_6_saída ));
  MUX2x1 mux2x1_7 (.a(\mux2x1_5_saída ), .b(\mux2x1_6_saída ), .Sel(C), .\Saída (out_12));
endmodule

// 2x1
module MUX2x1 (
  input  Sel,
  input  a,
  input  b,
  output \Saída 
);

  wire and_1_out, and_2_out, not_1_out;

  not not_1 (not_1_out, Sel);
  and and_1 (and_1_out, not_1_out, a);
  and and_2 (and_2_out, Sel, b);
  or or_1 (\Saída , and_1_out, and_2_out);
endmodule
