// Logisim project Tarefa-2tr-05-HugoBilleMartins.circ as structural Verilog: 1 circuit, main circuit main
module main (
  input  a,
  input  b,
  input  c,
  input  d,
  output out_5,
  output out_6,
  output out_7,
  output out_8
);

  wire and_1_out, and_2_out, and_3_out, and_4_out, and_5_out, and_6_out, and_7_out, and_8_out, not_1_out,
       not_2_out, not_3_out, not_4_out, or_1_out, or_2_out, or_3_out, or_4_out, or_5_out, or_6_out, or_7_out,
       or_8_out;

  not not_1 (not_1_out, a);
  not not_2 (not_2_out, b);
  not not_3 (not_3_out, c);
  not not_4 (not_4_out, d);
  and and_1 (and_1_out, b, not_4_out);
  or or_1 (or_1_out, b, not_4_out);
  and and_2 (and_2_out, d, not_2_out);
  or or_2 (or_2_out, d, not_2_out);
  and and_3 (and_3_out, not_4_out, b);
  or or_3 (or_3_out, not_4_out, b);
  and and_4 (and_4_out, d, not_3_out);
  or or_4 (or_4_out, d, not_3_out);
  and and_5 (and_5_out, or_1_out, not_3_out);
  and and_6 (and_6_out, or_2_out, c);
  and and_7 (and_7_out, or_3_out, c);
  and and_8 (and_8_out, or_4_out, not_2_out);
  or or_5 (or_5_out, and_1_out, and_5_out);
  or or_6 (or_6_out, and_2_out, and_6_out);
  or or_7 (or_7_out, and_3_out, and_7_out);
  or or_8 (or_8_out, and_4_out, and_8_out);
  and and_9 (out_5, or_5_out, not_1_out);
  and and_10 (out_6, or_6_out, not_1_out);
  and and_11 (out_7, or_7_out, not_1_out);
  and and_12 (out_8, or_8_out, not_1_out);
endmodule
